# Fritzing sketch circuito-principal-nano (saved by Fritzing 0.9.0b)
circuit board: 5.26816cm x 2.9163cm
breadboards: 1

parts:
  Componente1 = Arduino Nano (Rev3.0)
  J1 = female pin header, 2 pins [form="♀ (female)"]
  J2 = male pin header, 3 pins [form="♂ (male)"]
  J3 = male pin header, 3 pins [form="♂ (male)"]
  J4 = male pin header, 3 pins [form="♂ (male)"]
  J5 = male pin header, 3 pins [form="♂ (male)"]
  J6 = female pin header, 2 pins [form="♀ (female)"]
  J7 = female pin header, 2 pins [form="♀ (female)"]
  R1 = Resistor [tolerance=±5% resistance=220 package=THT]
  R2 = Resistor [tolerance=±5% resistance=220 package=THT]

nets:
  N1: Componente1.GND, J1.pin2, J4.pin1, J5.pin3, J6.pin1, J7.pin1
  N2: Componente1.D2, J4.pin2
  N3: Componente1.D3, J5.pin2
  N4: Componente1.D6, J3.pin1
  N5: Componente1.D7, J3.pin2
  N6: Componente1.D8, J3.pin3
  N7: Componente1.D10, J2.pin1
  N8: Componente1.D11/MOSI, J2.pin2
  N9: Componente1.D12/MISO, J2.pin3
  N10: Componente1.VIN, J1.pin1
  N11: Componente1.5V, J4.pin3, J5.pin1
  N12: Componente1.A7, R1.Pin_0
  N13: Componente1.A6, R2.Pin_0
  N14: J6.pin2, R1.Pin_1
  N15: J7.pin2, R2.Pin_1
