# Fritzing sketch circuito-principal (saved by Fritzing 0.9.0b)
circuit board: 8.46667cm x 5.64444cm
breadboards: 1

parts:
  Y1 = CRYSTAL [package=crystal-smd-10.5x4.8-2pin]  # not connected
  C1 = Capacitor [package=cap-pth-small-kit]  # not connected
  C2 = Capacitor [package=cap-pth-small-kit]  # not connected
  U1 = atmega328 [package=dip]
  S1 = Pushbutton [package="[THT]"]
  R1 = Resistor [tolerance=±5% resistance=220 package=THT]
  J1 = female pin header, 2 pins [form="♀ (female)"]
  JP1 = FTDI_BASIC [package=ftdi_basic]
  J2 = female pin header, 2 pins [form="♀ (female)"]
  J3 = female pin header, 2 pins [form="♀ (female)"]
  JP2 = FTDI_BASIC [package=ftdi_basic]

nets:
  N1: U1.RESET, S1.Pin_3, S1.Pin_4, R1.Pin_1
  N2: U1.D2, J2.pin2
  N3: U1.D3_(PWM), J3.pin1
  N4: U1.D4, JP1.5
  N5: U1.VCC, U1.AVCC, U1.AREF, R1.Pin_0, J1.pin1
  N6: U1.D5_(PWM), JP1.2
  N7: U1.D6_(PWM), JP2.3
  N8: U1.D7, JP2.2
  N9: U1.D8, JP2.1
  N10: U1.D9_(PWM), JP2.4
  N11: U1.D10_(PWM), JP2.5
  N12: U1.D11_(PWM), JP2.6
  N13: S1.Pin_1, S1.Pin_2
