# Fritzing sketch driver-motor (saved by Fritzing 0.9.0b)
circuit board: 2.33304cm x 2.55881cm
breadboards: 1

parts:
  S1 = Toggle Switch [package=THT]
  VCC5 = Battery
  VCC6 = Battery
  S2 = Toggle Switch [package=THT]
  VCC7 = Battery
  IC2 = L293D [package=THT]

nets:
  N1: S1.L1, IC2.Enable_2
  N2: S1.COM, IC2.In_3
  N3: S1.L2, IC2.In_4
  N4: VCC5.-, IC2.+Vmotor, IC2.+V
  N5: VCC5.+, IC2.0V
  N6: VCC6.-, IC2.Out_4_(_Controlled_by_Enable_2_)
  N7: VCC6.+, IC2.Out_3_(_Controlled_by_Enable_2_)
  N8: S2.L1, IC2.Enable_1
  N9: S2.COM, IC2.In_1
  N10: S2.L2, IC2.In_2
  N11: VCC7.-, IC2.Out_1_(_Controlled_by_Enable_1_)
  N12: VCC7.+, IC2.Out_2_(_Controlled_by_Enable_1_)
