# Fritzing sketch regulador-voltagem (saved by Fritzing 0.9.0b)
circuit board: 2.77519cm x 2.06022cm
breadboards: 1

parts:
  VCC3 = Battery
  C3 = Electrolytic Capacitor [capacitance=1µF package="100 mil [THT, electrolytic]"]
  C4 = Electrolytic Capacitor [capacitance=1µF package="100 mil [THT, electrolytic]"]
  LED2 = LED - 5mm [color="Red (633nm)" package="5 mm [THT]"]
  VCC4 = Battery
  S2 = Toggle Switch [package=THT]
  U2 = Voltage Regulator - 5V [package="TO220 [THT]"]
  R2 = Resistor [tolerance=±5% resistance=220 package=THT]

nets:
  N1: VCC3.-, C3.-, C4.-, LED2.cathode, VCC4.-, U2.GND
  N2: VCC3.+, S2.L2
  N3: C3.+, S2.COM, U2.input_voltage
  N4: C4.+, VCC4.+, U2.output_voltage, R2.Pin_1
  N5: LED2.anode, R2.Pin_0
