# Fritzing sketch shield-principal (saved by Fritzing 0.9.0b)
circuit board: 8.46667cm x 5.64444cm
breadboards: 1

parts:
  J1 = female pin header, 14 pins [form="♀ (female)"]
  J2 = female pin header, 6 pins [form="♀ (female)"]
  J3 = female pin header, 6 pins [form="♀ (female)"]
  J4 = female pin header, 6 pins [form="♀ (female)"]
  J5 = female pin header, 6 pins [form="♀ (female)"]
  J6 = male pin header, 4 pins [form="♂ (male)"]
  R1 = Resistor [tolerance=±5% resistance=220 package=THT]
  R2 = Resistor [tolerance=±5% resistance=220 package=THT]

nets:
  N1: J1.pin2, J5.pin1, J5.pin6, J6.pin1, J6.pin3
  N2: J1.pin4, J4.pin1
  N3: J1.pin5, J4.pin2
  N4: J1.pin6, J4.pin3
  N5: J1.pin9, J4.pin4
  N6: J1.pin10, J4.pin5
  N7: J1.pin11, J4.pin6
  N8: J2.pin3, J5.pin3, J5.pin4
  N9: J3.pin1, J5.pin5
  N10: J3.pin2, J5.pin2
  N11: J3.pin3, R1.Pin_0
  N12: J3.pin4, R2.Pin_0
  N13: J6.pin2, R1.Pin_1
  N14: J6.pin4, R2.Pin_1
